# Fritzing sketch beadsorter (saved by Fritzing 0.9.9b)
circuit board: 8.46667cm x 5.64444cm
breadboards: 1

parts:
  Bauteil1 = Arduino Nano (Rev3.0)
  Pololu_A1 = Pololu A4988 [package=SO16]
  M1 = Stepper Motor - Bipolar
  LED1 = LEDs [package=led10mm]
  R1 = PHOTOCELL [package=photocell]
  M2 = gear-motor
  J1 = Basic Servo
  Bauteil2 = Adafruit TCS34725 RGB Color Sensor [part_number="Adafruit #1334"]
  S1 = H-Bridge with L298N
  Power_plug1 = Power plug
  U1 = LM2596 step down module
  C1 = Capacitor Polarized [package=panasonic_e]
  U2 = LM2596 step down module
  S2 = Pushbutton [package=THT]
  R2 = Resistor [tolerance=±5% resistance=10k package="0402 [SMD]"]
  R3 = Resistor [tolerance=±5% resistance=10k package="0402 [SMD]"]
  R4 = Resistor [tolerance=±5% resistance=220 package="0402 [SMD]"]

nets:
  GND: Bauteil1.GND, Pololu_A1.GND, LED1.C, J1.gnd, Bauteil2.GND, S1.GND, Power_plug1.GND, U1.IN-, U1.OUT-, C1.-, U2.IN-, U2.OUT-, R3.Pin_1
  N1: Bauteil1.D2, Pololu_A1.DIR
  N2: Bauteil1.D3, Pololu_A1.STEP
  N3: Bauteil1.D5, S1.ENB
  N4: Bauteil1.D6, S1.IN4
  N5: Bauteil1.D7, S1.IN3
  N6: Bauteil1.D8, J1.pulse
  N7: Bauteil1.D11/MOSI, S2.leg1, R2.Pin_0
  VIN: Bauteil1.VIN, Pololu_A1.VDD, J1.vcc, U2.OUT+, R4.Pin_1
  5V: Bauteil1.5V, Pololu_A1.MS1, Pololu_A1.MS2, R1.P$1, Bauteil2.VIN, S2.leg0, R2.Pin_1
  N8: Bauteil1.A5, Bauteil2.SCL
  N9: Bauteil1.A4, Bauteil2.SDA
  N10: Bauteil1.A0, R1.P$2, R3.Pin_0
  N11: Pololu_A1.RESET, Pololu_A1.SLEEP
  N12: Pololu_A1.1B, M1.D
  N13: Pololu_A1.1A, M1.B
  N14: Pololu_A1.2A, M1.C
  N15: Pololu_A1.2B, M1.A
  N16: Pololu_A1.VMOT, Power_plug1.VCC, U1.IN+, C1.+, U2.IN+
  N17: LED1.A, R4.Pin_0
  N18: M2.pin_1, S1.M2-02
  N19: M2.pin_2, S1.M2-01
  N20: S1.12V, U1.OUT+

custom parts:
  Adafruit TCS34725 RGB Color Sensor: Your electronics can now see in dazzling color with this lovely color light sensor. We found the best color sensor on the market, the TCS34725, which has RGB and Clear light sensing elements. An IR blocking filter, integrated on-chip and localized to the color sensing photodiodes, minimizes the IR spectral component of the incoming light and allows color measurements to be made accurately. The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
  H-Bridge with L298N: h-bridge
  LM2596 step down module: LM2596 DC-DC step down power supply module 3 A.
